# Fritzing sketch meteo-home (saved by Fritzing 0.9.3b)
circuit board: 5cm x 7cm
breadboards: 1

parts:
  DHT1 = DHT22 Humidity and Temperature Sensor [part_number="DHT 22"]
  R1 = Resistor [tolerance=±5% resistance=10k package="2010 [SMD]"]
  Componente1 = Barometric Pressure Sensor - BMP180 Breakout (GY-68)
  U1 = NodeMCU V1.0

nets:
  VDD: DHT1.VDD, R1.Pin_1, Componente1.VCC, U1.Vin
  N1: DHT1.DATA, R1.Pin_0, U1.D4
  GND: DHT1.GND, Componente1.GND, U1.GND
  N2: Componente1.SCL, U1.D1
  N3: Componente1.SDA, U1.D2
  N4: U1.D0, U1.RST

custom parts:
  NodeMCU V1.0: ESP8266 based NodeMCU
